# Fritzing sketch pinball (saved by Fritzing 0.7.10b)
breadboards: 1

parts:
  Arduino2 = Arduino
  R1 = Resistor [tolerance=±5% resistance=220 package=THT]
  R2 = Resistor [tolerance=±5% resistance=220 package=THT]
  S1 = Pushbutton [package="[THT]"]
  S2 = Toggle Switch [package=THT]
  SPKR1 = Loudspeaker
  R3 = Resistor [tolerance=±5% resistance=220 package=THT]

nets:
  N1: Arduino2.GND, R2.Pin_0
  N2: Arduino2.D8, SPKR1.pin2, R3.Pin_1
  N3: Arduino2.D3, R2.Pin_1, S1.Pin_3, S1.Pin_4, S2.COM
  N4: Arduino2.D2, R1.Pin_0, S2.L1
  N5: SPKR1.pin1, R3.Pin_0
